# Fritzing sketch kaavio (saved by Fritzing 0.9.10b)
circuit board: 8.46667cm x 5.64444cm

parts:
  Part1 = Arduino Nano (Rev3.0)
  LED1 = 7-SEGMENT-4DIGIT-YOUNGSUN [package=7-segment-4digit-youngsun]
  J1 = Piezo Speaker
  SW1 = DIP Switch 8 Position [package=dipswitch-08]
  Part2 = RFID-RC522
  R1 = Resistor [tolerance=±5% power=0.25 resistance=220 package=THT]
  R2 = Resistor [tolerance=±5% power=0.25 resistance=220 package=THT]
  R3 = Resistor [tolerance=±5% power=0.25 resistance=220 package=THT]

nets:
  GND: Part1.GND, LED1.GND, J1.pin1, R2.Pin_1
  N1: Part1.D2, LED1.CLK
  N2: Part1.D3, LED1.DIO
  N3: Part1.D4, J1.pin2
  N4: Part1.D5, SW1.3, R1.Pin_0
  N5: Part1.D6, SW1.2, R3.Pin_0
  N6: Part1.D7, SW1.1, R2.Pin_0
  N7: Part1.D9, Part2.RST
  N8: Part1.D10, Part2.SDA
  N9: Part1.D11/MOSI, Part2.MOSI
  N10: Part1.D12/MISO, Part2.MISO
  5V: Part1.5V, LED1.5V, SW1.14
  3V3: Part1.3V3, Part2.3.3V
  N11: Part1.D13/SCK, Part2.SCK

custom parts:
  7-SEGMENT-4DIGIT-YOUNGSUN: This is a part for the 4-Digit 7-segment LEDs from Young Sun. Different from the Digikey LEDs, all 16 pins are used. The LONGPADS Variant is used for a test jig, but you may like it because there is more pad to solder to. If you are concerned about routing space, the standard works just fine though.
